// Logisim project Assignment_final.circ as structural Verilog: 1 circuit, main circuit main
module main (
  input  in_1,
  input  in_2,
  input  in_3,
  input  in_4,
  input  in_5,
  input  in_6,
  input  in_7,
  input  in_8,
  input  in_9,
  input  in_10,
  input  in_11,
  input  in_12,
  input  in_13
);

  wire clock_1_out, d_ff_1_qn, d_ff_7_q, d_ff_8_q, d_ff_9_q, multiplexer_1_out, multiplexer_2_out,
       multiplexer_3_out, multiplexer_4_out, multiplexer_5_out, multiplexer_6_out, multiplexer_7_out,
       multiplexer_9_out, not_1_out, xnor_1_out;
  wire [0:0] d_ff_6_q;
  wire [3:0] adder_1_out, adder_2_out, and_1_out, d_ff_2_q, multiplexer_8_out, xor_1_out;

  Clock clock_1 (.out(clock_1_out));
  D_Flip_Flop d_ff_1 (.clk(clock_1_out), .D(1'b1), .Qn(d_ff_1_qn));  // open: Q, preset, en, reset
  Multiplexer #(.enable("false")) multiplexer_1 (
    .in0(multiplexer_8_out[3]), .in1(in_1), .out(multiplexer_1_out), .sel(d_ff_1_qn));
  D_Flip_Flop d_ff_2 (.clk(clock_1_out), .D(multiplexer_1_out), .Q(d_ff_2_q[3]));  // open: Qn, preset, en, reset
  Multiplexer #(.enable("false")) multiplexer_2 (
    .in0(multiplexer_8_out[2]), .in1(in_2), .out(multiplexer_2_out), .sel(d_ff_1_qn));
  xnor xnor_1 (xnor_1_out, d_ff_2_q[3], in_13);
  D_Flip_Flop d_ff_3 (.clk(clock_1_out), .D(multiplexer_2_out), .Q(d_ff_2_q[2]));  // open: Qn, preset, en, reset
  Multiplexer #(.enable("false")) multiplexer_3 (
    .in0(multiplexer_8_out[1]), .in1(in_3), .out(multiplexer_3_out), .sel(d_ff_1_qn));
  xor xor_1 (xor_1_out[0], in_9, xnor_1_out);
  xor xor_2 (xor_1_out[1], in_10, xnor_1_out);
  xor xor_3 (xor_1_out[2], in_11, xnor_1_out);
  xor xor_4 (xor_1_out[3], in_13, xnor_1_out);
  not not_1 (not_1_out, xnor_1_out);
  D_Flip_Flop d_ff_4 (.clk(clock_1_out), .D(multiplexer_3_out), .Q(d_ff_2_q[1]));  // open: Qn, preset, en, reset
  Multiplexer #(.enable("false")) multiplexer_4 (
    .in0(multiplexer_8_out[0]), .in1(in_4), .out(multiplexer_4_out), .sel(d_ff_1_qn));
  and and_1 (and_1_out[0], in_9, not_1_out);
  and and_2 (and_1_out[1], in_10, not_1_out);
  and and_3 (and_1_out[2], in_11, not_1_out);
  and and_4 (and_1_out[3], in_13, not_1_out);
  D_Flip_Flop d_ff_5 (.clk(clock_1_out), .D(multiplexer_4_out), .Q(d_ff_2_q[0]));  // open: Qn, preset, en, reset
  Multiplexer #(.enable("false")) multiplexer_5 (.in0(d_ff_7_q), .in1(in_5), .out(multiplexer_5_out), .sel(d_ff_1_qn));
  Adder #(.width(4)) adder_1 (
    .a({d_ff_2_q[2:0], d_ff_6_q[0]}), .b(xor_1_out), .out(adder_1_out), .cin(xnor_1_out));  // open: cout
  D_Flip_Flop d_ff_6 (.clk(clock_1_out), .D(multiplexer_5_out), .Q(d_ff_6_q[0]));  // open: Qn, preset, en, reset
  Multiplexer #(.enable("false")) multiplexer_6 (.in0(d_ff_8_q), .in1(in_6), .out(multiplexer_6_out), .sel(d_ff_1_qn));
  Adder #(.width(4)) adder_2 (.a(d_ff_2_q), .b(and_1_out), .out(adder_2_out));  // open: cin, cout
  D_Flip_Flop d_ff_7 (.clk(clock_1_out), .D(multiplexer_6_out), .Q(d_ff_7_q));  // open: Qn, preset, en, reset
  Multiplexer #(.enable("false")) multiplexer_7 (.in0(d_ff_9_q), .in1(in_7), .out(multiplexer_7_out), .sel(d_ff_1_qn));
  Multiplexer #(.width(4), .enable("false")) multiplexer_8 (
    .in0(adder_1_out), .in1(adder_2_out), .out(multiplexer_8_out), .sel(in_12));
  D_Flip_Flop d_ff_8 (.clk(clock_1_out), .D(multiplexer_7_out), .Q(d_ff_8_q));  // open: Qn, preset, en, reset
  Multiplexer #(.enable("false")) multiplexer_9 (
    .in0(xnor_1_out), .in1(in_8), .out(multiplexer_9_out), .sel(d_ff_1_qn));
  D_Flip_Flop d_ff_9 (.clk(clock_1_out), .D(multiplexer_9_out), .Q(d_ff_9_q));  // open: Qn, preset, en, reset
endmodule
