// Logisim project aa1.circ as structural Verilog: 3 circuits, main circuit p1
module p1 (
  input  I4,
  input  I3,
  input  I2,
  input  I1,
  input  C2,
  input  C1,
  output B4,
  output B3,
  output B2,
  output B1
);

  wire and_1_out, and_2_out, and_3_out, and_4_out, and_5_out, and_6_out, and_7_out, and_8_out, and_9_out,
       and_10_out, and_11_out, and_12_out, and_13_out, and_14_out, and_15_out, and_16_out, and_17_out,
       and_18_out, and_19_out, not_1_out, not_2_out, not_3_out, not_4_out, not_5_out, not_6_out, not_7_out,
       not_8_out, not_9_out, not_10_out, not_11_out, not_12_out, xor_1_out, xor_2_out, xor_3_out, xor_4_out;

  not not_1 (not_1_out, I1);
  not not_2 (not_2_out, I2);
  xor xor_1 (xor_1_out, I3, I4);
  not not_3 (not_3_out, I2);
  not not_4 (not_4_out, I1);
  not not_5 (not_5_out, I3);
  not not_6 (not_6_out, I1);
  not not_7 (not_7_out, I2);
  not not_8 (not_8_out, I3);
  not not_9 (not_9_out, I3);
  ExactlyOne xor_2 (.out(xor_2_out), .in0(I2), .in1(I3), .in2(I4));
  xor xor_3 (xor_3_out, I1, I2);
  xor xor_4 (xor_4_out, xor_2_out, I1);
  not not_10 (not_10_out, I1);
  not not_11 (not_11_out, C2);
  not not_12 (not_12_out, C1);
  and and_1 (and_1_out, not_11_out, I4);
  and and_2 (and_2_out, C2, I3, I4);
  and and_3 (and_3_out, C2, not_12_out, I1, I2, I4);
  and and_4 (and_4_out, C2, C1, not_1_out, not_2_out, I4);
  and and_5 (and_5_out, not_11_out, not_12_out, I3);
  and and_6 (and_6_out, not_11_out, C1, xor_1_out);
  and and_7 (and_7_out, C2, not_12_out, I1, I2, I3);
  and and_8 (and_8_out, C2, not_12_out, I1, not_3_out, I4);
  and and_9 (and_9_out, C2, not_12_out, not_4_out, not_5_out, I4);
  and and_10 (and_10_out, C2, C1, not_6_out, not_7_out, I3);
  and and_11 (and_11_out, C2, C1, I1, not_8_out);
  and and_12 (and_12_out, C2, C1, I2, not_9_out);
  and and_13 (and_13_out, not_11_out, not_12_out, I2);
  and and_14 (and_14_out, not_11_out, C1, xor_2_out);
  and and_15 (and_15_out, C2, xor_3_out);
  and and_16 (and_16_out, not_11_out, not_12_out, I1);
  and and_17 (and_17_out, not_11_out, C1, xor_4_out);
  and and_18 (and_18_out, C2, not_12_out, not_10_out);
  and and_19 (and_19_out, C2, C1, I1);
  or or_1 (B4, and_1_out, and_2_out, and_3_out, and_4_out);
  or or_2 (B3, and_5_out, and_6_out, and_7_out, and_8_out, and_9_out, and_10_out, and_11_out, and_12_out);
  or or_3 (B2, and_13_out, and_14_out, and_15_out);
  or or_4 (B1, and_16_out, and_17_out, and_18_out, and_19_out);
endmodule

module main (
  input  I4,
  input  I3,
  input  I2,
  input  I1,
  input  C2,
  input  C1,
  input  S2,
  input  S1,
  output O4,
  output O3,
  output O2,
  output O1
);

  wire p1_1_b1, p1_1_b2, p1_1_b3, p1_1_b4;

  p1 p1_1 (
    .I4(I4), .I3(I3), .I2(I2), .I1(I1), .C2(C2), .C1(C1), .B4(p1_1_b4), .B3(p1_1_b3), .B2(p1_1_b2),
    .B1(p1_1_b1));
  p2 p2_1 (
    .B4(p1_1_b4), .B3(p1_1_b3), .B2(p1_1_b2), .B1(p1_1_b1), .S2(S2), .S1(S1), .O4(O4), .O3(O3), .O2(O2),
    .O1(O1));
endmodule

module p2 (
  input  B4,
  input  B3,
  input  B2,
  input  B1,
  input  S2,
  input  S1,
  output O4,
  output O3,
  output O2,
  output O1
);

  wire and_1_out, and_2_out, and_3_out, and_4_out, and_5_out, and_6_out, and_7_out, and_8_out, and_9_out,
       and_10_out, and_11_out, and_12_out, and_13_out, and_14_out, and_15_out, not_2_out, not_3_out,
       not_4_out, not_5_out, not_6_out, xnor_1_out, xor_1_out, xor_2_out, xor_3_out;

  // NOT_Gate not_1 has open pins: in=B4, out=open
  not not_2 (not_2_out, B2);
  not not_3 (not_3_out, B3);
  not not_4 (not_4_out, B1);
  xor xor_1 (xor_1_out, B2, B3);
  xor xor_2 (xor_2_out, B2, B1);
  xor xor_3 (xor_3_out, B2, B1);
  xnor xnor_1 (xnor_1_out, B2, B1);
  not not_5 (not_5_out, S1);
  not not_6 (not_6_out, S2);
  and and_1 (and_1_out, S2, B3, B1);
  and and_2 (and_2_out, S2, B3, B2);
  and and_3 (and_3_out, not_6_out, B3);
  and and_4 (and_4_out, not_6_out, S1, B4);
  and and_5 (and_5_out, S2, B3, not_2_out, not_4_out);
  and and_6 (and_6_out, S2, not_3_out, B1);
  and and_7 (and_7_out, S2, not_3_out, B2);
  and and_8 (and_8_out, not_6_out, not_5_out, B2);
  and and_9 (and_9_out, not_6_out, S1, xor_1_out);
  and and_10 (and_10_out, S2, not_5_out, xnor_1_out);
  and and_11 (and_11_out, S2, S1, xor_2_out);
  and and_12 (and_12_out, not_6_out, not_5_out, B1);
  and and_13 (and_13_out, not_6_out, S1, xor_3_out);
  and and_14 (and_14_out, S2, not_5_out, not_4_out);
  and and_15 (and_15_out, S2, S1, B1);
  or or_1 (O4, B4, and_1_out, and_2_out);
  or or_2 (O3, and_3_out, and_4_out, and_5_out, and_6_out, and_7_out);
  or or_3 (O2, and_8_out, and_9_out, and_10_out, and_11_out);
  or or_4 (O1, and_12_out, and_13_out, and_14_out, and_15_out);
  // OR_Gate or_5 is placed but not wired
endmodule
