// Logisim project 24bce174.circ as structural Verilog: 1 circuit, main circuit main
module main (
  input  in_1,
  input  in_2,
  input  in_3,
  input  in_4,
  input  in_5,
  input  in_6,
  input  in_7,
  input  in_8,
  input  in_9,
  input  in_10,
  output out_11,
  output out_12,
  output out_13,
  output out_14,
  output out_15,
  output out_16,
  output out_17,
  output out_18
);

  wire and_2_out, and_3_out, and_4_out, and_5_out, not_1_out, not_2_out, not_3_out, xor_2_out, xor_3_out;

  xor xor_1 (out_12, in_2, in_4);
  xor xor_2 (xor_2_out, in_6, in_7);
  not not_1 (not_1_out, in_2);
  not not_2 (not_2_out, in_6);
  xor xor_3 (xor_3_out, in_9, in_10);
  and and_1 (out_14, not_1_out, in_4);
  and and_2 (and_2_out, not_2_out, in_7);
  and and_3 (and_3_out, in_9, in_10);
  not not_3 (not_3_out, xor_2_out);
  xor xor_4 (out_15, in_5, xor_2_out);
  and and_4 (and_4_out, not_3_out, in_5);
  xor xor_5 (out_17, in_8, xor_3_out);
  and and_5 (and_5_out, xor_3_out, in_8);
  or or_1 (out_16, and_4_out, and_2_out);
  or or_2 (out_18, and_5_out, and_3_out);
  xor xor_6 (out_11, in_1, in_3);
  and and_6 (out_13, in_3, in_1);

  // Notes on the sheet:
  //   24BCE174
  //   Half Subtractor
  //   Full Subtractor
  //   Full Adder
  //   Practical 2 (A)
  //   Half Adder
endmodule
