// Logisim project Adder.circ as structural Verilog: 1 circuit, main circuit main
module main (
  input  A3,
  input  A2,
  input  A1,
  input  A0,
  input  B3,
  input  B2,
  input  B1,
  input  B0
);

  wire adder_1_cout, adder_3_cout, adder_5_cout, adder_7_cout, and_1_out, and_2_out;
  wire [3:0] adder_1_out, adder_3_out, adder_5_out, adder_7_out;
  wire [3:1] undriven, undriven_2, undriven_3, undriven_4, undriven_5, undriven_6, undriven_7, undriven_8;

  // OR_Gate or_1 has open pins: in0=adder_1_cout, in1=and_1_out, in2=and_2_out, out=open
  and and_1 (and_1_out, adder_1_out[0], adder_5_out[0]);
  and and_2 (and_2_out, adder_3_out[0], adder_1_out[0]);
  Adder #(.width(4)) adder_1 (
    .a({undriven, A3}), .b({undriven_2, B3}), .out(adder_1_out), .cin(adder_3_cout), .cout(adder_1_cout));
  Adder #(.width(4)) adder_2 (.cin(adder_1_out[0]));  // open: a, b, out, cout
  Adder #(.width(4)) adder_3 (
    .a({undriven_3, A2}), .b({undriven_4, B2}), .out(adder_3_out), .cin(adder_5_cout), .cout(adder_3_cout));
  Adder #(.width(4)) adder_4 ();  // open: a, b, out, cin, cout
  Adder #(.width(4)) adder_5 (
    .a({undriven_5, A1}), .b({undriven_6, B1}), .out(adder_5_out), .cin(adder_7_cout), .cout(adder_5_cout));
  Adder #(.width(4)) adder_6 ();  // open: a, b, out, cin, cout
  Adder #(.width(4)) adder_7 (
    .a({undriven_7, A0}), .b({undriven_8, B0}), .out(adder_7_out), .cout(adder_7_cout));  // open: cin
  Adder #(.width(4)) adder_8 ();  // open: a, b, out, cin, cout
  // Pins of 1 and 4 bits meet at {undriven, A3}
  // Pins of 1 and 4 bits meet at adder_3_out
  // Pins of 1 and 4 bits meet at adder_1_out
  // Pins of 1 and 4 bits meet at {undriven_5, A1}
  // Pins of 1 and 4 bits meet at {undriven_6, B1}
  // Pins of 1 and 4 bits meet at adder_5_out
  // Pins of 1 and 4 bits meet at {undriven_2, B3}
  // Pins of 1 and 4 bits meet at {undriven_3, A2}
  // Pins of 1 and 4 bits meet at {undriven_8, B0}
  // Pins of 1 and 4 bits meet at {undriven_4, B2}
  // Pins of 1 and 4 bits meet at {undriven_7, A0}
endmodule
