// Logisim project  P1 GATES USING NAND.circ as structural Verilog: 1 circuit, main circuit main
module main (
  input  in_1,
  input  in_2,
  input  in_3,
  input  in_4,
  input  in_5,
  input  in_6,
  input  in_7,
  input  in_8,
  input  in_9,
  input  in_10,
  input  in_11,
  output out_12,
  output out_13,
  output out_14,
  output out_15,
  output out_16,
  output out_17
);

  wire nand_1_out, nand_2_out, nand_3_out, nand_4_out, nand_6_out, nand_7_out, nand_8_out, nand_11_out,
       nand_12_out, nand_13_out, nand_14_out, nand_15_out, nand_18_out;

  nand nand_1 (nand_1_out, in_6, in_7);
  nand nand_2 (nand_2_out, in_8, in_8);
  nand nand_3 (nand_3_out, in_9, in_9);
  nand nand_4 (nand_4_out, in_10, in_11);
  nand nand_5 (out_12, in_1, in_1);
  nand nand_6 (nand_6_out, in_2, in_3);
  nand nand_7 (nand_7_out, in_4, in_4);
  nand nand_8 (nand_8_out, in_5, in_5);
  nand nand_9 (out_13, nand_6_out, nand_6_out);
  nand nand_10 (out_14, nand_7_out, nand_8_out);
  nand nand_11 (nand_11_out, in_6, nand_1_out);
  nand nand_12 (nand_12_out, nand_1_out, in_7);
  nand nand_13 (nand_13_out, nand_2_out, nand_3_out);
  nand nand_14 (nand_14_out, in_10, nand_4_out);
  nand nand_15 (nand_15_out, nand_4_out, in_11);
  nand nand_16 (out_15, nand_11_out, nand_12_out);
  nand nand_17 (out_16, nand_13_out, nand_13_out);
  nand nand_18 (nand_18_out, nand_14_out, nand_15_out);
  nand nand_19 (out_17, nand_18_out, nand_18_out);

  // Notes on the sheet:
  //   NOT using NAND
  //   OR using NAND
  //   NOR using NAND
  //   XNOR using NAND
  //   24BCE192-Practical-1
  //   AND using NAND
  //   XOR using NAND
endmodule
