// Logisim project P1 BASIC GATES.circ as structural Verilog: 1 circuit, main circuit main
module main (
  input  in_1,
  input  in_2,
  input  in_3,
  input  in_4,
  input  in_5,
  input  in_6,
  input  in_7,
  input  in_8,
  input  in_9,
  input  in_10,
  input  in_11,
  input  in_12,
  input  in_13,
  input  in_14,
  input  in_15,
  input  in_16,
  input  in_17,
  input  in_18,
  input  in_19,
  output out_20,
  output out_21,
  output out_22,
  output out_23,
  output out_24,
  output out_25,
  output out_26,
  output out_27,
  output out_28
);

  and and_1 (out_20, in_1, in_4);
  or or_1 (out_22, in_6, in_9);
  not not_1 (out_24, in_11);
  xor xor_1 (out_25, in_12, in_13);
  nand nand_1 (out_27, in_16, in_17);
  nor nor_1 (out_28, in_18, in_19);
  xnor xnor_1 (out_26, in_14, in_15);
  and and_2 (out_21, in_2, in_3, in_5);
  or or_2 (out_23, in_7, in_8, in_10);

  // Notes on the sheet:
  //   24BCE192
  //   Practical-1
endmodule
