// Logisim project P2 BINARY AND GRAY CODE.circ as structural Verilog: 1 circuit, main circuit main
module main (
  input  B3,
  input  G3,
  input  B2,
  input  G2,
  input  B1,
  input  G1,
  input  B0,
  input  G0,
  output G3_2,
  output B3_2,
  output G2_2,
  output B2_2,
  output G1_2,
  output B1_2,
  output G0_2,
  output B0_2
);

  xor xor_1 (G2_2, B3, B2);
  xor xor_2 (G1_2, B2, B1);
  xor xor_3 (G0_2, B1, B0);
  xor xor_4 (B2_2, G3, G2);
  xor xor_5 (B1_2, B2_2, G1);
  xor xor_6 (B0_2, B1_2, G0);

  assign B3_2 = G3;
  assign G3_2 = B3;

  // Notes on the sheet:
  //   Binary To Gray Code
  //   Gray Code To Binaray
endmodule
