// Logisim project P3 84-2-1 TO 5421.circ as structural Verilog: 1 circuit, main circuit main
module main (
  input  A,
  input  B,
  input  C,
  input  D,
  output W,
  output X,
  output Y,
  output Z
);

  wire A_prime_D_out, AB_out, AC_prime_out, AD_prime_out, BC_prime_D_prime_out, BCD_prime_out, C_prime_D_out,
       not_1_out, not_2_out, not_3_out;

  not not_1 (not_1_out, A);
  not not_2 (not_2_out, C);
  not not_3 (not_3_out, D);
  and AB (AB_out, A, B);
  and BC_prime_D_prime (BC_prime_D_prime_out, B, not_2_out, not_3_out);
  and AD_prime (AD_prime_out, not_3_out, A);
  and A_prime_D (A_prime_D_out, not_1_out, D);
  and AC_prime (AC_prime_out, A, not_2_out);
  and C_prime_D (C_prime_D_out, not_2_out, D);
  and BCD_prime (BCD_prime_out, B, C, not_3_out);
  or or_1 (Z, AD_prime_out, A_prime_D_out);
  or or_2 (X, AB_out, BC_prime_D_prime_out);
  or or_3 (Y, AC_prime_out, C_prime_D_out, BCD_prime_out);

  assign W = A;

  // Notes on the sheet:
  //   8 4 -2 -1  TO 5 4 2 1 Convertor
  //   AD'+A'D
  //   AB+BC'D'
  //   AC'+C'D+BCD'
endmodule
