// Logisim project P3 BCD TO 2421.circ as structural Verilog: 1 circuit, main circuit main
module main (
  input  P,
  input  Q,
  input  R,
  input  S,
  output A,
  output B,
  output C,
  output D
);

  wire not_1_out, not_2_out, not_3_out, Q_prime_R_out, QR_2_out, QR_out, QR_prime_S_out, QS_out, QS_prime_out;

  not not_1 (not_1_out, R);
  and QS (QS_out, Q, S);
  not not_2 (not_2_out, Q);
  not not_3 (not_3_out, S);
  and QR (QR_out, Q, R);
  and QR_2 (QR_2_out, Q, R);
  and QS_prime (QS_prime_out, Q, not_3_out);
  or or_1 (A, P, QS_out, QR_out);
  and Q_prime_R (Q_prime_R_out, not_2_out, R);
  and QR_prime_S (QR_prime_S_out, Q, not_1_out, S);
  or or_2 (B, P, QR_2_out, QS_prime_out);
  or or_3 (C, P, Q_prime_R_out, QR_prime_S_out);

  assign D = S;

  // Notes on the sheet:
  //   BCD TO 2 4 2 1 Convertor
  //   P+QS+QR
  //   P+QR+QS'
  //   P+QR+QR'S
endmodule
