// Logisim project P3 PARITY.circ as structural Verilog: 1 circuit, main circuit main
module main (
  input  A,
  input  B,
  input  C,
  input  D,
  input  E,
  input  F,
  input  G,
  input  A_2,
  input  B_2,
  input  C_2,
  input  D_2,
  input  E_2,
  input  F_2,
  input  G_2,
  input  P,
  output P_2,
  output PC
);

  wire xor_1_out, xor_2_out, xor_3_out, xor_4_out, xor_5_out, xor_6_out, xor_7_out, xor_8_out, xor_9_out,
       xor_10_out, xor_11_out, xor_12_out, xor_13_out;

  xor xor_1 (xor_1_out, A, B);
  xor xor_2 (xor_2_out, C, D);
  xor xor_3 (xor_3_out, E, F);
  xor xor_4 (xor_4_out, A_2, B_2);
  xor xor_5 (xor_5_out, C_2, D_2);
  xor xor_6 (xor_6_out, E_2, F_2);
  xor xor_7 (xor_7_out, G_2, P);
  xor xor_8 (xor_8_out, xor_1_out, xor_2_out);
  xor xor_9 (xor_9_out, xor_3_out, G);
  xor xor_10 (xor_10_out, xor_4_out, xor_5_out);
  xor xor_11 (xor_11_out, xor_6_out, xor_7_out);
  xor xor_12 (xor_12_out, xor_8_out, xor_9_out);
  xor xor_13 (xor_13_out, xor_10_out, xor_11_out);
  not not_1 (P_2, xor_12_out);
  not not_2 (PC, xor_13_out);

  // Notes on the sheet:
  //   4-BIT PARITY GENERATOR
  //   4-BIT PARITY CHECKER
endmodule
