// Logisim project P3 SQUARE.circ as structural Verilog: 1 circuit, main circuit main
module main (
  input  X,
  input  Y,
  input  Z,
  output A,
  output B,
  output C,
  output D,
  output E,
  output F
);

  wire and_2_out, and_3_out, and_4_out, and_5_out, not_1_out, not_2_out, not_3_out;

  not not_1 (not_1_out, X);
  and and_1 (A, X, Y);
  not not_2 (not_2_out, Y);
  and and_2 (and_2_out, X, not_2_out);
  and and_3 (and_3_out, X, Z);
  and and_4 (and_4_out, X, not_2_out, Z);
  and and_5 (and_5_out, not_1_out, Y, Z);
  not not_3 (not_3_out, Z);
  and and_6 (D, Y, not_3_out);
  or or_1 (C, and_4_out, and_5_out);
  or or_2 (B, and_2_out, and_3_out);

  assign E = 1'b0;
  assign F = Z;

  // Notes on the sheet:
  //   SQUARE OF 3-BIT NUMBER
endmodule
