// Logisim project LAB 10.circ as structural Verilog: 1 circuit, main circuit main
module main (
  input  [1:0] in_1,
  input  in_2,
  input  in_3
);

  wire clock_1_out, d_ff_1_q, d_ff_2_q, d_ff_3_q, d_ff_4_q, multiplexer_1_out, multiplexer_2_out,
       multiplexer_3_out, multiplexer_4_out, undriven, undriven_2;

  Clock clock_1 (.out(clock_1_out));
  D_Flip_Flop d_ff_1 (.clk(clock_1_out), .D(multiplexer_1_out), .Q(d_ff_1_q));  // open: Qn, preset, en, reset
  Multiplexer #(.select(2)) multiplexer_1 (
    .in0(d_ff_1_q), .in1(d_ff_2_q), .in2(in_3), .in3(undriven), .out(multiplexer_1_out), .sel(in_1));  // open: en
  Multiplexer #(.select(2)) multiplexer_2 (
    .in0(d_ff_2_q), .in1(d_ff_3_q), .in2(d_ff_1_q), .in3(undriven), .out(multiplexer_2_out), .sel(in_1));  // open: en
  D_Flip_Flop d_ff_2 (.clk(clock_1_out), .D(multiplexer_2_out), .Q(d_ff_2_q));  // open: Qn, preset, en, reset
  D_Flip_Flop d_ff_3 (.clk(clock_1_out), .D(multiplexer_3_out), .Q(d_ff_3_q));  // open: Qn, preset, en, reset
  Multiplexer #(.select(2)) multiplexer_3 (
    .in0(d_ff_3_q), .in1(d_ff_4_q), .in2(d_ff_2_q), .in3(undriven), .out(multiplexer_3_out), .sel(in_1));  // open: en
  Multiplexer #(.select(2)) multiplexer_4 (
    .in0(d_ff_4_q), .in1(undriven_2), .in2(d_ff_3_q), .in3(undriven), .out(multiplexer_4_out), .sel(in_1));  // open: en
  D_Flip_Flop d_ff_4 (.clk(clock_1_out), .D(multiplexer_4_out), .Q(d_ff_4_q));  // open: Qn, preset, en, reset
endmodule
