// Logisim project PRACTICAL 1A.circ as structural Verilog: 1 circuit, main circuit main
module main (
  input  A,
  input  A_2,
  input  B,
  input  B_2,
  input  A_3,
  input  A_4,
  input  B_3,
  input  B_4,
  input  A_5,
  input  A_6,
  input  B_5,
  input  B_6,
  input  A_7,
  output out_14,
  output out_15,
  output out_16,
  output Y__A_B__prime,
  output out_18,
  output out_19,
  output out_20
);

  and AND (out_14, A, B);
  or OR (out_16, A_3, B_3);
  xnor XNOR (out_18, A_5, B_5);
  not not_1 (out_20, A_7);
  nand NAND (out_15, A_2, B_2);
  nor NOR (Y__A_B__prime, A_4, B_4);
  xor XOR (out_19, A_6, B_6);

  // Notes on the sheet:
  //         Y=(A.B + (A.B)')'
  //                       Y=A'
  //   Y=A.B                                
  //   Y=A+B                               
  //   NOT        
  //                    Y=A.B + (A.B)'
  //   Y=(A.B)'
endmodule
