// Logisim project PRACTICAL 1B.circ as structural Verilog: 1 circuit, main circuit main
module main (
  input  A,
  input  A_2,
  input  A_3,
  input  A_4,
  input  B,
  input  B_2,
  input  A_5,
  input  A_6,
  input  B_3,
  input  B_4,
  input  A_7,
  input  A_8,
  input  B_5,
  input  B_6,
  input  A_9,
  input  A_10,
  input  B_7,
  input  B_8,
  output Y_A_prime,
  output Y_A_prime_2,
  output Y_A_B,
  output Y_A_B_2,
  output Y_A_B_3,
  output Y_A_B_4,
  output Y_A_B_prime___A_prime_B,
  output Y_A_B_prime___A_prime_B_2,
  output Y__A_B_prime___A_prime_B__prime,
  output Y__A_B_prime___A_prime_B__prime_2
);

  wire nand_1_out, nand_2_out, nand_3_out, nand_4_out, nand_5_out, nand_7_out, nand_8_out, nand_9_out,
       nand_10_out, nand_14_out, nor_1_out, nor_2_out, nor_3_out, nor_4_out, nor_5_out, nor_9_out,
       nor_10_out, nor_11_out, nor_12_out, nor_13_out;

  nand nand_1 (nand_1_out, A_3, B);
  nand nand_2 (nand_2_out, A_5, A_5);
  nand nand_3 (nand_3_out, B_4, B_4);
  nand nand_4 (nand_4_out, A_7, B_5);
  nand nand_5 (nand_5_out, A_10, B_8);
  nand nand_6 (Y_A_prime, A, A);
  nand nand_7 (nand_7_out, A_7, nand_4_out);
  nand nand_8 (nand_8_out, nand_4_out, B_5);
  nand nand_9 (nand_9_out, A_10, nand_5_out);
  nand nand_10 (nand_10_out, nand_5_out, B_8);
  nand nand_11 (Y_A_B, nand_1_out, nand_1_out);
  nand nand_12 (Y_A_B_4, nand_2_out, nand_3_out);
  nand nand_13 (Y_A_B_prime___A_prime_B, nand_7_out, nand_8_out);
  nand nand_14 (nand_14_out, nand_9_out, nand_10_out);
  nand nand_15 (Y__A_B_prime___A_prime_B__prime_2, nand_14_out, nand_14_out);
  nor nor_1 (nor_1_out, A_4, A_4);
  nor nor_2 (nor_2_out, B_2, B_2);
  nor nor_3 (nor_3_out, A_6, B_3);
  nor nor_4 (nor_4_out, A_8, B_6);
  nor nor_5 (nor_5_out, A_9, B_7);
  nor nor_6 (Y_A_prime_2, A_2, A_2);
  nor nor_7 (Y_A_B_2, nor_1_out, nor_2_out);
  nor nor_8 (Y_A_B_3, nor_3_out, nor_3_out);
  nor nor_9 (nor_9_out, A_8, nor_4_out);
  nor nor_10 (nor_10_out, nor_4_out, B_6);
  nor nor_11 (nor_11_out, A_9, nor_5_out);
  nor nor_12 (nor_12_out, nor_5_out, B_7);
  nor nor_13 (nor_13_out, nor_9_out, nor_10_out);
  nor nor_14 (Y__A_B_prime___A_prime_B__prime, nor_11_out, nor_12_out);
  nor nor_15 (Y_A_B_prime___A_prime_B_2, nor_13_out, nor_13_out);

  // Notes on the sheet:
  //   NOT GATE
  //   AND GATE
  //   OR GATE
  //   X-OR GATE
  //   X-NOR GATE
  //   NAND GATE
  //                                    NOR GATE
endmodule
