// Logisim project PRACTICAL 4.circ as structural Verilog: 1 circuit, main circuit main
module main (
  input  in_1,
  input  in_2,
  input  in_3,
  input  in_4,
  input  in_5,
  input  in_6,
  input  in_7,
  input  in_8,
  output out_9,
  output out_10,
  output out_11,
  output out_12,
  output out_13
);

  wire adder_1_cout, adder_1_out, adder_3_cout, adder_3_out, adder_4_cout, adder_5_cout, adder_5_out,
       adder_6_cout, adder_7_cout, adder_7_out, adder_8_cout, and_1_out, or_1_out, or_2_out;

  and and_1 (and_1_out, or_2_out, adder_1_out);
  or or_1 (or_1_out, adder_1_cout, and_1_out);
  or or_2 (or_2_out, adder_3_out, adder_5_out);
  Adder #(.width(1)) adder_1 (.a(in_1), .b(in_5), .out(adder_1_out), .cin(adder_3_cout), .cout(adder_1_cout));
  Adder #(.width(1)) adder_2 (.a(adder_1_out), .b(or_1_out), .out(out_10), .cin(adder_4_cout), .cout(out_9));
  Adder #(.width(1)) adder_3 (.a(in_2), .b(in_6), .out(adder_3_out), .cin(adder_5_cout), .cout(adder_3_cout));
  Adder #(.width(1)) adder_4 (.a(adder_3_out), .b(or_1_out), .out(out_11), .cin(adder_6_cout), .cout(adder_4_cout));
  Adder #(.width(1)) adder_5 (.a(in_3), .b(in_7), .out(adder_5_out), .cin(adder_7_cout), .cout(adder_5_cout));
  Adder #(.width(1)) adder_6 (.a(adder_5_out), .b(or_1_out), .out(out_12), .cin(adder_8_cout), .cout(adder_6_cout));
  Adder #(.width(1)) adder_7 (.a(in_4), .b(in_8), .out(adder_7_out), .cin(1'b0), .cout(adder_7_cout));
  Adder #(.width(1)) adder_8 (.a(adder_7_out), .b(or_1_out), .out(out_13), .cout(adder_8_cout));  // open: cin
endmodule
