// Logisim project Prac_5_DE(8x1).circ as structural Verilog: 1 circuit, main circuit main
module main (
  input  in_1,
  input  in_2,
  input  in_3,
  input  [2:0] in_4
);

  wire and_1_out, not_1_out, or_1_out;

  not not_1 (not_1_out, in_2);
  and and_1 (and_1_out, in_2, in_3);
  or or_1 (or_1_out, not_1_out, in_3);
  Multiplexer #(.select(3)) multiplexer_1 (
    .in0(and_1_out), .in1(in_1), .in2(in_3), .in3(or_1_out), .in4(and_1_out), .in5(in_1), .in6(and_1_out),
    .in7(and_1_out), .sel(in_4));  // open: out, en
endmodule
