// Logisim project Prac_5_DE.circ as structural Verilog: 1 circuit, main circuit main
module main (
  input  in_1,
  input  in_2,
  input  [3:0] in_3,
  output out_4
);

  wire not_1_out;

  not not_1 (not_1_out, in_2);
  not not_2 (not_1_out, in_1);
  Multiplexer #(.select(4)) multiplexer_1 (
    .in0(in_1), .in1(in_1), .in2(in_1), .in3(not_1_out), .in4(in_1), .in5(in_1), .in6(in_1), .in7(in_1),
    .in8(not_1_out), .in9(in_1), .in10(not_1_out), .in11(not_1_out), .in12(not_1_out), .in13(in_1),
    .in14(not_1_out), .in15(in_1), .out(out_4), .sel(in_3));  // open: en
endmodule
