// Logisim project Practical 0.circ as structural Verilog: 1 circuit, main circuit main
module main (
  input  [1:0] in_1,
  input  in_2,
  input  in_3,
  input  in_4,
  input  in_5,
  input  in_6,
  input  in_7,
  output out_8,
  output out_9,
  output out_10,
  output out_11
);

  wire clock_1_out, multiplexer_1_out, multiplexer_2_out, multiplexer_3_out, multiplexer_4_out;

  Clock clock_1 (.out(clock_1_out));
  D_Flip_Flop d_ff_1 (.clk(clock_1_out), .D(multiplexer_1_out), .Q(out_8));  // open: Qn, preset, en, reset
  Multiplexer #(.select(2)) multiplexer_1 (
    .in0(in_4), .in1(in_2), .in2(in_3), .in3(out_8), .out(multiplexer_1_out), .sel(in_1));  // open: en
  D_Flip_Flop d_ff_2 (.clk(clock_1_out), .D(multiplexer_2_out), .Q(out_9));  // open: Qn, preset, en, reset
  Multiplexer #(.select(2)) multiplexer_2 (
    .in0(in_7), .in1(in_2), .in2(out_8), .in3(out_9), .out(multiplexer_2_out), .sel(in_1));  // open: en
  D_Flip_Flop d_ff_3 (.clk(clock_1_out), .D(multiplexer_3_out), .Q(out_10));  // open: Qn, preset, en, reset
  Multiplexer #(.select(2)) multiplexer_3 (
    .in0(in_5), .in1(in_2), .in2(out_8), .in3(out_10), .out(multiplexer_3_out), .sel(in_1));  // open: en
  D_Flip_Flop d_ff_4 (.clk(clock_1_out), .D(multiplexer_4_out), .Q(out_11));  // open: Qn, preset, en, reset
  Multiplexer #(.select(2)) multiplexer_4 (
    .in0(in_6), .in1(in_2), .in2(out_8), .in3(out_11), .out(multiplexer_4_out), .sel(in_1));  // open: en

  // Notes on the sheet:
  //   00 - parallel change
  //   01 - left shift
  //   10 - right shift
  //   11 - no change
endmodule
