// Logisim project Practical 8.circ as structural Verilog: 1 circuit, main circuit main
module main (
);

  wire and_1_out, clock_1_out, j_k_ff_1_q, j_k_ff_2_q, j_k_ff_4_q, not_1_out, not_2_out, or_1_out, or_2_out,
       or_3_out, xor_1_out, xor_2_out;

  Clock clock_1 (.out(clock_1_out));
  J_K_Flip_Flop j_k_ff_1 (.J(and_1_out), .clk(clock_1_out), .Q(j_k_ff_1_q));  // open: K, Qn, preset, en, reset
  and and_1 (and_1_out, j_k_ff_1_q, xor_1_out);
  xor xor_1 (xor_1_out, j_k_ff_2_q, j_k_ff_4_q);
  J_K_Flip_Flop j_k_ff_2 (.J(not_1_out), .clk(clock_1_out), .Q(j_k_ff_2_q));  // open: K, Qn, preset, en, reset
  not not_1 (not_1_out, or_1_out);
  or or_1 (or_1_out, j_k_ff_1_q, j_k_ff_4_q);
  J_K_Flip_Flop j_k_ff_3 (.J(or_2_out), .clk(clock_1_out), .Q(j_k_ff_1_q));  // open: K, Qn, preset, en, reset
  or or_2 (or_2_out, j_k_ff_1_q, not_2_out);
  J_K_Flip_Flop j_k_ff_4 (.J(or_3_out), .clk(clock_1_out), .Q(j_k_ff_4_q));  // open: K, Qn, preset, en, reset
  not not_2 (not_2_out, j_k_ff_4_q);
  or or_3 (or_3_out, j_k_ff_1_q, xor_2_out);
  xor xor_2 (xor_2_out, j_k_ff_1_q, j_k_ff_2_q);
endmodule
