// Logisim project Practical3-a.circ as structural Verilog: 1 circuit, main circuit main
module main (
  input  X,
  input  Y,
  input  Z,
  output A,
  output B,
  output C,
  output D,
  output E,
  output F
);

  wire AND_out, NOT_2_out, NOT_out, OR_out, XOR_out;

  and AND (AND_out, Y, Z);
  not NOT (NOT_out, Y);
  xor XOR (XOR_out, X, Y);
  not NOT_2 (NOT_2_out, Z);
  or OR (OR_out, NOT_out, AND_out);
  and AND_2 (A, X, Y);
  and ANd_3 (B, X, OR_out);
  and AND_4 (C, XOR_out, Z);
  and AND_5 (D, Y, NOT_2_out);
  and AND_6 (E, NOT_2_out, Z);

  assign F = Z;
endmodule
